// Logisim project meio_somador_proj.circ as structural Verilog: 1 circuit, main circuit main
module main (
  input  A0,
  input  B0,
  output SOMA,
  output Carry_out
);

  xor xor_1 (SOMA, A0, B0);
  and and_1 (Carry_out, A0, B0);
endmodule
