// Logisim project ula_4bits.circ as structural Verilog: 3 circuits, main circuit main
module main (
  input  [3:0] A,
  input  [3:0] B,
  input  bit_invert,
  input  [1:0] op_code,
  output [3:0] out_5,
  output carry_out
);

  wire ula_1_1_carry_out, ula_1_2_carry_out, ula_1_3_carry_out;

  ULA_1 ula_1_1 (
    .A(A[0]), .B(B[0]), .resultado(out_5[0]), .carry_in(bit_invert), .bit_invert(bit_invert),
    .carry_out(ula_1_1_carry_out), .op_code(op_code));
  ULA_1 ula_1_2 (
    .A(A[1]), .B(B[1]), .resultado(out_5[1]), .carry_in(ula_1_1_carry_out), .bit_invert(bit_invert),
    .carry_out(ula_1_2_carry_out), .op_code(op_code));
  ULA_1 ula_1_3 (
    .A(A[2]), .B(B[2]), .resultado(out_5[2]), .carry_in(ula_1_2_carry_out), .bit_invert(bit_invert),
    .carry_out(ula_1_3_carry_out), .op_code(op_code));
  ULA_1 ula_1_4 (
    .A(A[3]), .B(B[3]), .resultado(out_5[3]), .carry_in(ula_1_3_carry_out), .bit_invert(bit_invert),
    .carry_out(carry_out), .op_code(op_code));
endmodule

// +
module somador (
  input  A0,
  input  B0,
  input  Ci0,
  output S0,
  output Co0
);

  wire and_1_out, and_2_out, xor_1_out;

  xor xor_1 (xor_1_out, A0, B0);
  and and_1 (and_1_out, A0, B0);
  xor xor_2 (S0, xor_1_out, Ci0);
  and and_2 (and_2_out, xor_1_out, Ci0);
  or or_1 (Co0, and_2_out, and_1_out);
endmodule

// ULA
module ULA_1 (
  input  carry_in,
  input  A,
  input  B,
  input  [1:0] op_code,
  input  bit_invert,
  output resultado,
  output carry_out
);

  wire and_1_out, multiplexer_1_out, not_1_out, not_2_out, or_1_out, somador_1_s0;

  not not_1 (not_1_out, B);
  Multiplexer #(.enable("false")) multiplexer_1 (.in0(B), .in1(not_1_out), .out(multiplexer_1_out), .sel(bit_invert));
  and and_1 (and_1_out, A, multiplexer_1_out);
  or or_1 (or_1_out, A, multiplexer_1_out);
  not not_2 (not_2_out, A);
  somador somador_1 (.A0(A), .B0(multiplexer_1_out), .Ci0(carry_in), .S0(somador_1_s0), .Co0(carry_out));
  Multiplexer #(.select(2), .enable("false")) multiplexer_2 (
    .in0(and_1_out), .in1(or_1_out), .in2(not_2_out), .in3(somador_1_s0), .out(resultado), .sel(op_code));
endmodule
