// Logisim project ula_74LS181.circ as structural Verilog: 3 circuits, main circuit main
module main (
  input  [3:0] A,
  input  [3:0] B,
  input  [3:0] op_code,
  output [3:0] saida
);

  wire [3:0] and_1_out, and_2_out, and_3_out, nand_1_out, nor_1_out, not_1_out, not_2_out, not_3_out,
       not_4_out, not_5_out, not_6_out, or_1_out, or_2_out, or_3_out, xnor_1_out, xor_1_out;

  assign not_1_out = ~A;  // NOT_Gate not_1, 4 bits wide
  assign not_2_out = ~A;  // NOT_Gate not_2, 4 bits wide
  assign not_3_out = ~B;  // NOT_Gate not_3, 4 bits wide
  assign xor_1_out = A ^ B;  // XOR_Gate xor_1, 4 bits wide
  assign not_4_out = ~B;  // NOT_Gate not_4, 4 bits wide
  assign not_5_out = ~A;  // NOT_Gate not_5, 4 bits wide
  assign and_1_out = A & B;  // AND_Gate and_1, 4 bits wide
  assign not_6_out = ~B;  // NOT_Gate not_6, 4 bits wide
  assign nor_1_out = ~(A | B);  // NOR_Gate nor_1, 4 bits wide
  assign and_2_out = not_2_out & B;  // AND_Gate and_2, 4 bits wide
  assign nand_1_out = ~(A & B);  // NAND_Gate nand_1, 4 bits wide
  assign and_3_out = A & not_4_out;  // AND_Gate and_3, 4 bits wide
  assign or_1_out = not_5_out | B;  // OR_Gate or_1, 4 bits wide
  assign xnor_1_out = ~(A ^ B);  // XNOR_Gate xnor_1, 4 bits wide
  assign or_2_out = A | not_6_out;  // OR_Gate or_2, 4 bits wide
  assign or_3_out = A | B;  // OR_Gate or_3, 4 bits wide
  Multiplexer #(.select(4), .width(4), .enable("false")) multiplexer_1 (
    .in0(not_1_out), .in1(nor_1_out), .in2(and_2_out), .in3(4'b0000), .in4(nand_1_out), .in5(not_3_out),
    .in6(xor_1_out), .in7(and_3_out), .in8(or_1_out), .in9(xnor_1_out), .in10(B), .in11(and_1_out),
    .in12(4'b0001), .in13(or_2_out), .in14(or_3_out), .in15(A), .out(saida), .sel(op_code));
endmodule

// +
module somador (
  input  A0,
  input  B0,
  input  Ci0,
  output S0,
  output Co0
);

  wire and_1_out, and_2_out, xor_1_out;

  xor xor_1 (xor_1_out, A0, B0);
  and and_1 (and_1_out, A0, B0);
  xor xor_2 (S0, xor_1_out, Ci0);
  and and_2 (and_2_out, xor_1_out, Ci0);
  or or_1 (Co0, and_2_out, and_1_out);
endmodule

// ULA
module ULA_1 (
  input  carry_in,
  input  A,
  input  B,
  input  [1:0] op_code,
  input  bit_invert,
  output resultado,
  output carry_out
);

  wire and_1_out, multiplexer_1_out, not_1_out, not_2_out, or_1_out, somador_1_s0;

  not not_1 (not_1_out, B);
  Multiplexer #(.enable("false")) multiplexer_1 (.in0(B), .in1(not_1_out), .out(multiplexer_1_out), .sel(bit_invert));
  and and_1 (and_1_out, A, multiplexer_1_out);
  or or_1 (or_1_out, A, multiplexer_1_out);
  not not_2 (not_2_out, A);
  somador somador_1 (.A0(A), .B0(multiplexer_1_out), .Ci0(carry_in), .S0(somador_1_s0), .Co0(carry_out));
  Multiplexer #(.select(2), .enable("false")) multiplexer_2 (
    .in0(and_1_out), .in1(or_1_out), .in2(not_2_out), .in3(somador_1_s0), .out(resultado), .sel(op_code));
endmodule
