// Logisim project somador_completo.circ as structural Verilog: 1 circuit, main circuit main
module main (
  input  A0,
  input  B0,
  input  Ci0,
  output S0,
  output Co0
);

  wire and_1_out, and_2_out, xor_1_out;

  xor xor_1 (xor_1_out, A0, B0);
  and and_1 (and_1_out, A0, B0);
  xor xor_2 (S0, xor_1_out, Ci0);
  and and_2 (and_2_out, xor_1_out, Ci0);
  or or_1 (Co0, and_2_out, and_1_out);
endmodule
